# Fritzing sketch Sensors_and_Monitoring_Systems_final_project (saved by Fritzing 1.0.7)
breadboards: 1

parts:
  S1 = Pushbutton [package="[THT]"]
  Adafruit_Simple_Soil_Moisture_Sensor1 = Adafruit Simple Soil Moisture Sensor [mn=Adafruit mpn=#6362 part_number=#6362]
  Part2 = Adafruit HUZZAH ESP8266 [part_number="Adafruit #2471"]

nets:
  N1: S1.Pin_1, S1.Pin_2, Part2.GPIO5
  GND: S1.Pin_3, S1.Pin_4, Adafruit_Simple_Soil_Moisture_Sensor1.GND, Part2.GND
  N2: Adafruit_Simple_Soil_Moisture_Sensor1.V+, Part2.3.3V
  N3: Adafruit_Simple_Soil_Moisture_Sensor1.SIGNAL, Part2.ADC
